# Fritzing sketch xbeeLiPo (saved by Fritzing 0.9.2b)
breadboards: 1

parts:
  U1 = XBee
  S1 = Pushbutton [package="[THT]"]
  S2 = Toggle Switch [package=THT]
  LED1 = smd LED [color="Green (555nm)" package="1206 [SMD]"]
  R1 = Resistor [tolerance=±5% resistance=330 package=THT]
  パーツ1 = Power Cell LiPo Charger/Booster
  U3 = LIPO-1000mAh [package=lipo-1000]

nets:
  N1: U1.VCC, S2.L2, R1.Pin_0
  N2: U1.GND, S1.Pin_1, S1.Pin_2, S2.L1, LED1.cathode
  N3: U1.pin11, S1.Pin_3, S1.Pin_4
  N4: LED1.anode, R1.Pin_1
  N5: パーツ1.VBATT, U3.+
  N6: パーツ1.GND, U3.-
